# Fritzing sketch EL-wire Digital Switch (saved by Fritzing 0.8.3b)
circuit board: 2.77514cm x 3.65006cm
breadboards: 1

parts:
  R1 = Resistor [tolerance=±5% resistance=220 package=THT]
  JP1 = Header 2 [package=jst-2-pth-ns]
  JP3 = Header 3 [package=jst-3-pth]
  JP2 = Header 2 [package=jst-2-pth-ns]
  U1 = MOC3023 [package=dil06]
  U3 = TRIAC [package=to-92]

nets:
  N1: R1.Pin_0, U1.4
  N2: R1.Pin_1, JP1.1, U3.M1
  N3: JP1.2, JP2.2
  N4: JP3.1, U1.2
  N5: JP3.2, U1.1
  N6: JP2.1, U3.M2
  N7: U1.6, U3.G

custom parts:
  MOC3023: Opto-isolated TRIAC
